# Fritzing sketch sim-setup1 (saved by Fritzing 0.9.4)
breadboards: 1

parts:
  Part1 = Arduino Micro (Rev3)
  SIM800L_BO1 = SIM800L BO
  ANT1 = Antenna
  R1 = Resistor [tolerance=±5% resistance=20k package=THT]
  R2 = Resistor [tolerance=±5% resistance=10k package=THT]
  M1 = RioRand LM2596

nets:
  N1: Part1.D8_PWM/A8, R2.Pin_0
  N2: Part1.D9_PWM/A9, SIM800L_BO1.pin_5
  N3: Part1.GND, M1.Pin_2
  N4: Part1.5V, M1.Pin_1
  N5: SIM800L_BO1.PIN1, ANT1.antenna_lead
  N6: SIM800L_BO1.PIN2, M1.Pin_3
  N7: SIM800L_BO1.pin_4, R1.Pin_0, R2.Pin_1
  N8: SIM800L_BO1.pin_6, R1.Pin_1, M1.Pin_4
